// Logisim project 三种触发器.circ as structural Verilog: 1 circuit, main circuit main
module main (
  input  in_1,
  input  in_2,
  input  in_3,
  input  in_4,
  input  in_5
);

  wire clock_1_out, clock_2_out, clock_3_out, d_ff_1_qn, j_k_ff_1_q, s_r_ff_1_q;

  Clock clock_1 (.out(clock_1_out));
  Clock clock_2 (.out(clock_2_out));
  Clock clock_3 (.out(clock_3_out));
  S_R_Flip_Flop s_r_ff_1 (.S(in_1), .clk(clock_1_out), .R(in_2), .Q(s_r_ff_1_q));  // open: Qn, preset, reset
  LED led_1 (.in(s_r_ff_1_q));
  J_K_Flip_Flop j_k_ff_1 (.J(in_3), .clk(clock_2_out), .K(in_4), .Q(j_k_ff_1_q));  // open: Qn, preset, reset
  LED led_2 (.in(j_k_ff_1_q));
  D_Flip_Flop d_ff_1 (.clk(clock_3_out), .D(in_5), .Qn(d_ff_1_qn));  // open: Q, preset, reset
  LED led_3 (.in(d_ff_1_qn));
endmodule
