// Logisim project 实验一 多数决.circ as structural Verilog: 2 circuits, main circuit L_6f90e275
// Bool
module L_6f90e275 (
  input  A,
  input  B,
  input  C,
  output F
);

  wire and_1_out, and_2_out, and_3_out, and_4_out, and_5_out, and_6_out, and_7_out, and_8_out, and_9_out,
       and_10_out, and_11_out, not_1_out, not_2_out, not_3_out, not_4_out, not_5_out, not_6_out, not_7_out;

  and and_1 (and_1_out, A, B);
  not not_1 (not_1_out, C);
  and and_2 (and_2_out, A, B);
  not not_2 (not_2_out, B);
  and and_3 (and_3_out, not_2_out, A);
  not not_3 (not_3_out, A);
  and and_4 (and_4_out, not_3_out, B);
  and and_5 (and_5_out, and_1_out, C);
  not not_4 (not_4_out, and_5_out);
  and and_6 (and_6_out, not_1_out, and_2_out);
  not not_5 (not_5_out, and_6_out);
  and and_7 (and_7_out, and_3_out, C);
  not not_6 (not_6_out, and_7_out);
  and and_8 (and_8_out, and_4_out, C);
  not not_7 (not_7_out, and_8_out);
  and and_9 (and_9_out, not_4_out, not_5_out);
  and and_10 (and_10_out, not_6_out, not_7_out);
  and and_11 (and_11_out, and_9_out, and_10_out);
  not not_8 (F, and_11_out);
endmodule

// sTruth
module L_68fb15ca (
  input  X1,
  input  X0,
  input  Y1,
  input  Y0,
  output Gt
);


  // Notes on the sheet:
  //   输入引脚
  //   请勿增加、删除引脚，用隧道标签构建电路
  //   请勿更改电路封装外观
  //   输出引脚
endmodule
