// Logisim project 8-3.circ as structural Verilog: 1 circuit, main circuit main
module main (
  input  I0,
  input  I1,
  input  I2,
  input  I3,
  input  I4,
  input  I5,
  input  I6,
  input  I7,
  output O3,
  output O2,
  output O1
);

  wire and_1_out, and_2_out, and_3_out, and_4_out, and_5_out, and_6_out, and_7_out, and_8_out, and_9_out,
       and_10_out, and_11_out, and_12_out, not_1_out, not_2_out, not_3_out, not_4_out, not_5_out, not_6_out,
       not_7_out, not_8_out, not_9_out, not_10_out, not_11_out, not_12_out;

  and and_1 (and_1_out, I0, ~I1, ~I2, ~I3, ~I4, ~I5, ~I6, ~I7);  // AND_Gate
  and and_2 (and_2_out, ~I0, I1, ~I2, ~I3, ~I4, ~I5, ~I6, ~I7);  // AND_Gate
  and and_3 (and_3_out, ~I0, ~I1, I2, ~I3, ~I4, ~I5, ~I6, ~I7);  // AND_Gate
  and and_4 (and_4_out, ~I0, ~I1, ~I2, I3, ~I4, ~I5, ~I6, ~I7);  // AND_Gate
  and and_5 (and_5_out, I0, ~I1, ~I2, ~I3, ~I4, ~I5, ~I6, ~I7);  // AND_Gate
  and and_6 (and_6_out, ~I0, I1, ~I2, ~I3, ~I4, ~I5, ~I6, ~I7);  // AND_Gate
  and and_7 (and_7_out, ~I0, ~I1, ~I2, ~I3, I4, ~I5, ~I6, ~I7);  // AND_Gate
  and and_8 (and_8_out, ~I0, ~I1, ~I2, ~I3, ~I4, I5, ~I6, ~I7);  // AND_Gate
  and and_9 (and_9_out, I0, ~I1, ~I2, ~I3, ~I4, ~I5, ~I6, ~I7);  // AND_Gate
  and and_10 (and_10_out, ~I0, ~I1, I2, ~I3, ~I4, ~I5, ~I6, ~I7);  // AND_Gate
  and and_11 (and_11_out, ~I0, ~I1, ~I2, ~I3, I4, ~I5, ~I6, ~I7);  // AND_Gate
  and and_12 (and_12_out, ~I0, ~I1, ~I2, ~I3, ~I4, ~I5, I6, ~I7);  // AND_Gate
  not not_1 (not_1_out, and_1_out);
  not not_2 (not_2_out, and_2_out);
  not not_3 (not_3_out, and_3_out);
  not not_4 (not_4_out, and_4_out);
  not not_5 (not_5_out, and_5_out);
  not not_6 (not_6_out, and_6_out);
  not not_7 (not_7_out, and_7_out);
  not not_8 (not_8_out, and_8_out);
  not not_9 (not_9_out, and_9_out);
  not not_10 (not_10_out, and_10_out);
  not not_11 (not_11_out, and_11_out);
  not not_12 (not_12_out, and_12_out);
  and and_13 (O3, not_1_out, not_2_out, not_3_out, not_4_out);
  and and_14 (O2, not_5_out, not_6_out, not_7_out, not_8_out);
  and and_15 (O1, not_9_out, not_10_out, not_11_out, not_12_out);
  Hex_Digit_Display hex_digit_display_1 ();  // open: value, dp
endmodule
