// Logisim project 实验三 74ls283.circ as structural Verilog: 2 circuits, main circuit main
module main (
  input  [7:0] in_1,
  input  [7:0] in_2
);

  wire l_283_510f6660_1_l_0b3b22ab, l_283_510f6660_2_l_0b3b22ab;
  wire [3:0] l_283_510f6660_1_l_4_eaf24e6a, l_283_510f6660_2_l_4_eaf24e6a;

  Hex_Digit_Display hex_digit_display_1 (.value(in_1[7:4]));  // open: dp
  Hex_Digit_Display hex_digit_display_2 (.value(in_2[7:4]));  // open: dp
  Hex_Digit_Display hex_digit_display_3 (.value(in_1[3:0]));  // open: dp
  Hex_Digit_Display hex_digit_display_4 (.value(in_2[3:0]));  // open: dp
  Hex_Digit_Display hex_digit_display_5 (.value(l_283_510f6660_2_l_4_eaf24e6a));  // open: dp
  L_283_510f6660 l_283_510f6660_1 (
    .L_0b3b22ab(l_283_510f6660_1_l_0b3b22ab), .L_4_eaf24e6a(l_283_510f6660_1_l_4_eaf24e6a), .A3(in_1[3]),
    .A2(in_1[2]), .A1(in_1[1]), .A0(in_1[0]), .B3(in_2[3]), .B2(in_2[2]), .B1(in_2[1]), .B0(in_2[0]));  // open: L_68f87a01
  Hex_Digit_Display hex_digit_display_6 (.value(l_283_510f6660_1_l_4_eaf24e6a));  // open: dp
  L_283_510f6660 l_283_510f6660_2 (
    .L_0b3b22ab(l_283_510f6660_2_l_0b3b22ab), .L_4_eaf24e6a(l_283_510f6660_2_l_4_eaf24e6a), .A3(in_1[7]),
    .A2(in_1[6]), .A1(in_1[5]), .A0(in_1[4]), .L_68f87a01(l_283_510f6660_1_l_0b3b22ab), .B3(in_2[7]),
    .B2(in_2[6]), .B1(in_2[5]), .B0(in_2[4]));
  LED led_1 (.in(l_283_510f6660_2_l_0b3b22ab));
endmodule

module L_283_510f6660 (
  input  A3,
  input  A2,
  input  A1,
  input  A0,
  input  B3,
  input  B2,
  input  B1,
  input  B0,
  input  L_68f87a01,
  output [3:0] L_4_eaf24e6a,
  output L_0b3b22ab
);

  _74283 #(.ShowInternalStructure("true")) u_74283_1 (
    .pin1(L_4_eaf24e6a[1]), .pin2(B1), .pin3(A1), .pin4(L_4_eaf24e6a[0]), .pin5(A0), .pin6(B0),
    .pin7(L_68f87a01), .pin15(B2), .pin14(A2), .pin13(L_4_eaf24e6a[2]), .pin12(A3), .pin11(B3),
    .pin10(L_4_eaf24e6a[3]), .pin9(L_0b3b22ab));
endmodule
