// Logisim project 实验二：全加器.circ as structural Verilog: 2 circuits, main circuit FA
module FA (
  input  CI,
  input  A,
  input  B,
  output S,
  output CO
);

  wire and_1_out, and_2_out, xor_1_out;

  and and_1 (and_1_out, A, B);
  xor xor_1 (xor_1_out, A, B);
  and and_2 (and_2_out, xor_1_out, CI);
  xor xor_2 (S, CI, xor_1_out);
  or or_1 (CO, and_2_out, and_1_out);
endmodule

module L_4FA_ce94afde (
  input  CI,
  input  [3:0] A,
  input  [3:0] B,
  output [3:0] S,
  output CO
);

  wire fa_1_co, fa_2_co, fa_3_co;

  Hex_Digit_Display hex_digit_display_1 (.value(S));  // open: dp
  Hex_Digit_Display hex_digit_display_2 (.value(A));  // open: dp
  Hex_Digit_Display hex_digit_display_3 (.value(B));  // open: dp
  FA fa_1 (.CI(CI), .A(A[0]), .B(B[0]), .S(S[0]), .CO(fa_1_co));
  FA fa_2 (.CI(fa_1_co), .A(A[1]), .B(B[1]), .S(S[1]), .CO(fa_2_co));
  FA fa_3 (.CI(fa_2_co), .A(A[2]), .B(B[2]), .S(S[2]), .CO(fa_3_co));
  FA fa_4 (.CI(fa_3_co), .A(A[3]), .B(B[3]), .S(S[3]), .CO(CO));
endmodule
